# Fritzing sketch transistor_switch (saved by Fritzing 0.9.0b)
breadboards: 1

parts:
  Raspberry_Pi1 = Raspberry Pi B rev2
  Q1 = NPN-Transistor [package="TO92 [THT]"]
  Q2 = NPN-Transistor [package="TO92 [THT]"]
  R1 = Resistor [tolerance=±5% resistance=1k package=THT]
  R2 = Resistor [tolerance=±5% resistance=1k package=THT]

nets:
  N1: Raspberry_Pi1.GPIO_23, Raspberry_Pi1.GND, Q1.E, Q2.E, R1.Pin_0
  N2: Raspberry_Pi1.GPIO_25, R2.Pin_1
  N3: Q1.B, R2.Pin_0
  N4: Q1.C, Q2.C
  N5: Q2.B, R1.Pin_1

notes:
  Ground wire
  Focus wire
  Release wire
